# Fritzing sketch Schematic (saved by Fritzing 0.9.1b)
stripboards: 1

parts:
  Part1 = Electric Imp April
  LED1 = LEDs [package=led10mm]
  LED2 = LEDs [package=led10mm]
  R5 = PHOTOCELL [package=photocell]
  J1 = Piezo Speaker
  R6 = Resistor [tolerance=±5% resistance=1k package=THT]
  VCC1 = Battery
  R7 = Resistor [tolerance=±5% resistance=47 package="1206 [SMD]"]
  R8 = Resistor [tolerance=±5% resistance=47 package="1206 [SMD]"]
  R9 = Resistor [tolerance=±5% resistance=47 package="1206 [SMD]"]
  R10 = Resistor [tolerance=±5% resistance=47 package="1206 [SMD]"]

nets:
  N1: Part1.1, R8.Pin_0
  N2: Part1.2, R7.Pin_0
  N3: Part1.3, R5.P$2
  N4: Part1.4, R9.Pin_0
  N5: Part1.5, R10.Pin_0
  N6: Part1.6, J1.pin2
  N7: Part1.8, R6.Pin_1
  N8: Part1.9, J1.pin1
  N9: Part1.12, Part1.13
  N10: Part1.15, VCC1.-
  N11: Part1.16, VCC1.+
  N12: LED1.A, R7.Pin_1
  N13: LED1.C, R8.Pin_1
  N14: LED2.A, R10.Pin_1
  N15: LED2.C, R9.Pin_1
  N16: R5.P$1, R6.Pin_0

custom parts:
  Electric Imp April: Electric Imp Breakout Board with onboard 3.3V regulated power supply
